// Logisim project krets.circ as structural Verilog: 3 circuits, main circuit main
module main (
  input  Sign,
  input  a,
  input  b,
  input  c,
  input  d,
  output Sign_bit,
  output A_2,
  output B_2,
  output C_2,
  output D_2,
  output E,
  output F,
  output G,
  output H
);

  wire _2er_kompl_a0, _2er_kompl_a1, _2er_kompl_b1, _2er_kompl_c1, _2er_kompl_d1, _2er_kompl_e1,
       _2er_kompl_f1, _2er_kompl_g1, _2er_kompl_h1, and_2_out, c1_out, c2_out, c3_out, c4_out,
       selector_1__2_s_comp, selector_1_vanlig, selector_2__2_s_comp, selector_2_vanlig,
       selector_3__2_s_comp, selector_3_vanlig, selector_4__2_s_comp, selector_4_vanlig,
       selector_5__2_s_comp, selector_5_vanlig, selector_6__2_s_comp, selector_6_vanlig,
       selector_7__2_s_comp, selector_7_vanlig, selector_8__2_s_comp, selector_8_vanlig, xor_1_out,
       xor_2_out, xor_3_out, xor_4_out, xor_5_out;

  and and_1 (Sign_bit, Sign, _2er_kompl_a0);
  and c4 (c4_out, c3_out, a);
  Selector selector_1 (.A(c4_out), .S(Sign), ._2_s_comp(selector_1__2_s_comp), .vanlig(selector_1_vanlig));
  or or_1 (A_2, selector_1_vanlig, _2er_kompl_a1);
  and c3 (c3_out, b, c2_out);
  xor xor_1 (xor_1_out, a, c3_out);
  Selector selector_2 (.A(xor_1_out), .S(Sign), ._2_s_comp(selector_2__2_s_comp), .vanlig(selector_2_vanlig));
  or or_2 (B_2, selector_2_vanlig, _2er_kompl_b1);
  xor xor_2 (xor_2_out, a, c);
  and and_2 (and_2_out, a, c);
  and c2 (c2_out, and_2_out, c1_out);
  xor xor_3 (xor_3_out, c2_out, b);
  Selector selector_3 (.A(xor_3_out), .S(Sign), ._2_s_comp(selector_3__2_s_comp), .vanlig(selector_3_vanlig));
  or or_3 (C_2, selector_3_vanlig, _2er_kompl_c1);
  and c1 (c1_out, d, b);
  xor xor_4 (xor_4_out, xor_2_out, c1_out);
  Selector selector_4 (.A(xor_4_out), .S(Sign), ._2_s_comp(selector_4__2_s_comp), .vanlig(selector_4_vanlig));
  or or_4 (D_2, selector_4_vanlig, _2er_kompl_d1);
  xor xor_5 (xor_5_out, b, d);
  Selector selector_5 (.A(xor_5_out), .S(Sign), ._2_s_comp(selector_5__2_s_comp), .vanlig(selector_5_vanlig));
  _2_s_comp _2er_kompl (
    .H(selector_8__2_s_comp), .G(selector_7__2_s_comp), .F(selector_6__2_s_comp), .E(selector_5__2_s_comp),
    .D(selector_4__2_s_comp), .C(selector_3__2_s_comp), .B(selector_2__2_s_comp), .A(selector_1__2_s_comp),
    .H1(_2er_kompl_h1), .G1(_2er_kompl_g1), .F1(_2er_kompl_f1), .E1(_2er_kompl_e1), .D1(_2er_kompl_d1),
    .C1(_2er_kompl_c1), .B1(_2er_kompl_b1), .A1(_2er_kompl_a1), .A0(_2er_kompl_a0));
  or or_5 (E, _2er_kompl_e1, selector_5_vanlig);
  Selector selector_6 (.A(c), .S(Sign), ._2_s_comp(selector_6__2_s_comp), .vanlig(selector_6_vanlig));
  or or_6 (F, _2er_kompl_f1, selector_6_vanlig);
  Selector selector_7 (.A(d), .S(Sign), ._2_s_comp(selector_7__2_s_comp), .vanlig(selector_7_vanlig));
  or or_7 (G, _2er_kompl_g1, selector_7_vanlig);
  Selector selector_8 (.A(1'b0), .S(Sign), ._2_s_comp(selector_8__2_s_comp), .vanlig(selector_8_vanlig));
  or or_8 (H, _2er_kompl_h1, selector_8_vanlig);

  // Notes on the sheet:
  //   aXORc3
  //   bXORc2
  //   aXORcXORc1
  //   bXORd
  //   Select-delen velger enten 2er komplement (når Sign er 1) eller
  //   lar bittene fra multiplikasjonen gjennom til utgangene A-H (Sign = 0)
endmodule

module Selector (
  input  A,
  input  S,
  output _2_s_comp,
  output vanlig
);

  wire not_1_out;

  not not_1 (not_1_out, S);
  and and_1 (_2_s_comp, A, S);
  and and_2 (vanlig, A, not_1_out);
endmodule

module _2_s_comp (
  input  H,
  input  G,
  input  F,
  input  E,
  input  D,
  input  C,
  input  B,
  input  A,
  output H1,
  output G1,
  output F1,
  output E1,
  output D1,
  output C1,
  output B1,
  output A1,
  output A0
);

  wire C1_out, C2_out, C3_out, C4_out, C5_out, C6_out, C7_out, not_1_out, not_2_out, not_3_out, not_4_out,
       not_5_out, not_6_out, not_7_out, not_8_out;

  not not_1 (not_1_out, H);
  not not_2 (not_2_out, G);
  not not_3 (not_3_out, F);
  not not_4 (not_4_out, E);
  not not_5 (not_5_out, D);
  not not_6 (not_6_out, C);
  not not_7 (not_7_out, B);
  not not_8 (not_8_out, A);
  xor xor_1 (H1, 1'b1, not_1_out);
  and u_C1 (C1_out, 1'b1, not_1_out);
  xor xor_2 (G1, C1_out, not_2_out);
  and C2 (C2_out, C1_out, not_2_out);
  xor xor_3 (F1, C2_out, not_3_out);
  and C3 (C3_out, C2_out, not_3_out);
  xor xor_4 (E1, C3_out, not_4_out);
  and C4 (C4_out, C3_out, not_4_out);
  xor xor_5 (D1, C4_out, not_5_out);
  and C5 (C5_out, C4_out, not_5_out);
  xor xor_6 (C1, C5_out, not_6_out);
  and C6 (C6_out, C5_out, not_6_out);
  xor xor_7 (B1, C6_out, not_7_out);
  and C7 (C7_out, C6_out, not_7_out);
  xor xor_8 (A1, C7_out, not_8_out);
  and C8 (A0, C7_out, not_8_out);
endmodule
