// Logisim project krets_.circ as structural Verilog: 4 circuits, main circuit main
module main (
  input  a,
  input  b,
  input  c,
  input  d,
  input  Sign,
  output Sign_bit,
  output A_2,
  output B_2,
  output C_2,
  output D_2,
  output E,
  output F,
  output G,
  output H
);

  wire multipl_1_a_2, multipl_1_b_2, multipl_1_c_2, multipl_1_d_2, multipl_1_e, multipl_1_f, multipl_1_g,
       multipl_1_h, n2_s_comp_1_a0, n2_s_comp_1_a1, n2_s_comp_1_b1, n2_s_comp_1_c1, n2_s_comp_1_d1,
       n2_s_comp_1_e1, n2_s_comp_1_f1, n2_s_comp_1_g1, n2_s_comp_1_h1, selector_1__2_s_comp,
       selector_1_vanlig, selector_2__2_s_comp, selector_2_vanlig, selector_3__2_s_comp, selector_3_vanlig,
       selector_4__2_s_comp, selector_4_vanlig, selector_5__2_s_comp, selector_5_vanlig,
       selector_6__2_s_comp, selector_6_vanlig, selector_7__2_s_comp, selector_7_vanlig,
       selector_8__2_s_comp, selector_8_vanlig;

  and and_1 (Sign_bit, Sign, n2_s_comp_1_a0);
  Selector selector_1 (.A(multipl_1_a_2), .S(Sign), ._2_s_comp(selector_1__2_s_comp), .vanlig(selector_1_vanlig));
  or or_1 (A_2, selector_1_vanlig, n2_s_comp_1_a1);
  Selector selector_2 (.A(multipl_1_b_2), .S(Sign), ._2_s_comp(selector_2__2_s_comp), .vanlig(selector_2_vanlig));
  or or_2 (B_2, selector_2_vanlig, n2_s_comp_1_b1);
  multipl multipl_1 (
    .a(a), .b(b), .c(c), .d(d), .A_2(multipl_1_a_2), .B_2(multipl_1_b_2), .C_2(multipl_1_c_2),
    .D_2(multipl_1_d_2), .E(multipl_1_e), .F(multipl_1_f), .G(multipl_1_g), .H(multipl_1_h));
  Selector selector_3 (.A(multipl_1_c_2), .S(Sign), ._2_s_comp(selector_3__2_s_comp), .vanlig(selector_3_vanlig));
  or or_3 (C_2, selector_3_vanlig, n2_s_comp_1_c1);
  Selector selector_4 (.A(multipl_1_d_2), .S(Sign), ._2_s_comp(selector_4__2_s_comp), .vanlig(selector_4_vanlig));
  or or_4 (D_2, selector_4_vanlig, n2_s_comp_1_d1);
  Selector selector_5 (.A(multipl_1_e), .S(Sign), ._2_s_comp(selector_5__2_s_comp), .vanlig(selector_5_vanlig));
  _2_s_comp u_2_s_comp_1 (
    .H(selector_8__2_s_comp), .G(selector_7__2_s_comp), .F(selector_6__2_s_comp), .E(selector_5__2_s_comp),
    .D(selector_4__2_s_comp), .C(selector_3__2_s_comp), .B(selector_2__2_s_comp), .A(selector_1__2_s_comp),
    .H1(n2_s_comp_1_h1), .G1(n2_s_comp_1_g1), .F1(n2_s_comp_1_f1), .E1(n2_s_comp_1_e1), .D1(n2_s_comp_1_d1),
    .C1(n2_s_comp_1_c1), .B1(n2_s_comp_1_b1), .A1(n2_s_comp_1_a1), .A0(n2_s_comp_1_a0));
  or or_5 (E, n2_s_comp_1_e1, selector_5_vanlig);
  Selector selector_6 (.A(multipl_1_f), .S(Sign), ._2_s_comp(selector_6__2_s_comp), .vanlig(selector_6_vanlig));
  or or_6 (F, n2_s_comp_1_f1, selector_6_vanlig);
  Selector selector_7 (.A(multipl_1_g), .S(Sign), ._2_s_comp(selector_7__2_s_comp), .vanlig(selector_7_vanlig));
  or or_7 (G, n2_s_comp_1_g1, selector_7_vanlig);
  Selector selector_8 (.A(multipl_1_h), .S(Sign), ._2_s_comp(selector_8__2_s_comp), .vanlig(selector_8_vanlig));
  or or_8 (H, n2_s_comp_1_h1, selector_8_vanlig);
endmodule

// Sel
module Selector (
  input  A,
  input  S,
  output _2_s_comp,
  output vanlig
);

  wire not_1_out;

  not not_1 (not_1_out, S);
  and and_1 (_2_s_comp, A, S);
  and and_2 (vanlig, A, not_1_out);
endmodule

// 2er kompl.
module _2_s_comp (
  input  H,
  input  G,
  input  F,
  input  E,
  input  D,
  input  C,
  input  B,
  input  A,
  output H1,
  output G1,
  output F1,
  output E1,
  output D1,
  output C1,
  output B1,
  output A1,
  output A0
);

  wire C1_out, C2_out, C3_out, C4_out, C5_out, C6_out, C7_out, not_1_out, not_2_out, not_3_out, not_4_out,
       not_5_out, not_6_out, not_7_out, not_8_out;

  not not_1 (not_1_out, H);
  not not_2 (not_2_out, G);
  not not_3 (not_3_out, F);
  not not_4 (not_4_out, E);
  not not_5 (not_5_out, D);
  not not_6 (not_6_out, C);
  not not_7 (not_7_out, B);
  not not_8 (not_8_out, A);
  xor xor_1 (H1, 1'b1, not_1_out);
  and u_C1 (C1_out, 1'b1, not_1_out);
  xor xor_2 (G1, C1_out, not_2_out);
  and C2 (C2_out, C1_out, not_2_out);
  xor xor_3 (F1, C2_out, not_3_out);
  and C3 (C3_out, C2_out, not_3_out);
  xor xor_4 (E1, C3_out, not_4_out);
  and C4 (C4_out, C3_out, not_4_out);
  xor xor_5 (D1, C4_out, not_5_out);
  and C5 (C5_out, C4_out, not_5_out);
  xor xor_6 (C1, C5_out, not_6_out);
  and C6 (C6_out, C5_out, not_6_out);
  xor xor_7 (B1, C6_out, not_7_out);
  and C7 (C7_out, C6_out, not_7_out);
  xor xor_8 (A1, C7_out, not_8_out);
  and C8 (A0, C7_out, not_8_out);
endmodule

module multipl (
  input  a,
  input  b,
  input  c,
  input  d,
  output A_2,
  output B_2,
  output C_2,
  output D_2,
  output E,
  output F,
  output G,
  output H
);

  wire and_1_out, and_2_out, and_3_out, and_4_out, and_5_out, and_6_out, and_7_out, and_8_out, and_9_out,
       and_10_out, and_11_out, and_12_out, and_13_out, and_14_out, and_15_out, and_16_out, and_17_out,
       not_1_out, not_2_out, not_3_out, not_4_out;

  and and_1 (and_1_out, a, b, d);
  and and_2 (and_2_out, a, b, c);
  or u_A (A_2, and_1_out, and_2_out);
  not not_1 (not_1_out, a);
  not not_2 (not_2_out, b);
  not not_3 (not_3_out, c);
  not not_4 (not_4_out, d);
  and and_3 (and_3_out, a, not_2_out);
  and and_4 (and_4_out, a, not_3_out, not_4_out);
  or u_B (B_2, and_3_out, and_4_out, and_5_out);
  and and_5 (and_5_out, not_1_out, b, c, d);
  and and_6 (and_6_out, b, not_3_out, not_4_out);
  and and_7 (and_7_out, not_1_out, b, not_3_out);
  or u_C (C_2, and_7_out, and_6_out, and_9_out, and_8_out);
  and and_8 (and_8_out, not_1_out, b, not_4_out);
  and and_9 (and_9_out, a, not_2_out, c);
  and and_10 (and_10_out, a, not_2_out, not_3_out);
  and and_11 (and_11_out, not_1_out, not_2_out, c);
  and and_12 (and_12_out, a, not_3_out, not_4_out);
  and and_13 (and_13_out, not_1_out, c, not_4_out);
  or u_D (D_2, and_11_out, and_10_out, and_13_out, and_12_out, and_14_out, and_15_out);
  and and_14 (and_14_out, not_1_out, b, not_3_out, d);
  and and_15 (and_15_out, a, b, c, d);
  and and_16 (and_16_out, not_2_out, d);
  and and_17 (and_17_out, not_4_out, b);
  or u_E (E, and_16_out, and_17_out);

  assign F = c;
  assign G = d;
  assign H = 1'b0;

  // Notes on the sheet:
  //   a'
  //   c'
  //   b'
  //   a
  //   d'
  //   b
  //   c
  //   d
endmodule
