// Logisim project oblig2.circ as structural Verilog: 3 circuits, main circuit main
module main (
  input  clr
);

  wire clock_1_out, inst_dek_datam_enable, inst_dek_progr_minne__enable, inst_dek_r_enable,
       inst_dek_ram_store, or_1_out;
  wire [1:0] inst_dek_reg__select;
  wire [3:0] adder_1_out, PC_q, ram_2_data;
  wire [7:0] controlled_buffer_1_out, R_q, ram_1_data, reg_sel_out;
  wire [7:4] ram_2_data_2;

  or or_1 (or_1_out, adder_1_out[0], adder_1_out[1], adder_1_out[2], adder_1_out[3]);
  Register #(.width(4)) PC (.D(adder_1_out), .en(or_1_out), .Q(PC_q), .clk(clock_1_out), .clr(clr));
  Adder #(.width(4)) adder_1 (.a(4'b0001), .b(PC_q), .out(adder_1_out));  // open: cin, cout
  Clock clock_1 (.out(clock_1_out));
  reg_selector reg_sel (.databus(controlled_buffer_1_out), .Q(R_q), .sel(inst_dek_reg__select), .out(reg_sel_out));
  assign controlled_buffer_1_out = inst_dek_r_enable ? R_q : 8'bz;  // Controlled_Buffer controlled_buffer_1
  Register R (.D(reg_sel_out), .Q(R_q), .clk(clock_1_out), .clr(clr));  // open: en
  RAM #(.addrWidth(4), .bus("separate")) ram_1 (
    .addr(ram_2_data), .din(controlled_buffer_1_out), .data(ram_1_data), .str(inst_dek_ram_store),
    .clk(clock_1_out), .clr(clr));  // open: sel, ld
  assign controlled_buffer_1_out = inst_dek_datam_enable ? ram_1_data : 8'bz;  // Controlled_Buffer controlled_buffer_2
  assign controlled_buffer_1_out = inst_dek_progr_minne__enable ? {ram_2_data_2, ram_2_data} : 8'bz;  // Controlled_Buffer controlled_buffer_3
  RAM #(.addrWidth(4)) ram_2 (.addr(PC_q), .data({ram_2_data_2, ram_2_data}), .clk(clock_1_out));  // open: sel, ld, clr
  instruksjonsdekoder inst_dek (
    .in_1(ram_2_data_2), .RAM_store(inst_dek_ram_store), .progr_minne__enable(inst_dek_progr_minne__enable),
    .datam_enable(inst_dek_datam_enable), .R_enable(inst_dek_r_enable), .Reg__select(inst_dek_reg__select));

  // Notes on the sheet:
  //   adder
  //   dataminne
  //   programminne
endmodule

module instruksjonsdekoder (
  input  [3:0] in_1,
  output RAM_store,
  output progr_minne__enable,
  output datam_enable,
  output R_enable,
  output [1:0] Reg__select
);

  wire and_1_out, and_2_out, and_3_out, and_4_out;
  wire [3:0] not_1_out;

  assign not_1_out = ~in_1;  // NOT_Gate not_1, 4 bits wide
  or or_1 (Reg__select[1], not_1_out[3], in_1[2], in_1[1]);
  and and_1 (and_1_out, in_1[3], not_1_out[2], not_1_out[1], in_1[0]);
  and and_2 (and_2_out, in_1[3], not_1_out[2], in_1[1], not_1_out[0]);
  and and_3 (and_3_out, in_1[3], not_1_out[2], not_1_out[1], not_1_out[0]);
  and and_4 (and_4_out, in_1[3], not_1_out[2], not_1_out[1], in_1[0]);
  or or_2 (Reg__select[0], and_1_out, and_2_out);
  and and_5 (RAM_store, in_1[3], not_1_out[2], in_1[1], in_1[0]);
  or or_3 (progr_minne__enable, and_3_out, and_4_out);
  and and_6 (datam_enable, in_1[3], not_1_out[2], in_1[1], not_1_out[0]);
  and and_7 (R_enable, in_1[3], not_1_out[2], in_1[1], in_1[0]);
endmodule

module reg_selector (
  input  [7:0] databus,
  input  [7:0] Q,
  input  [1:0] sel,
  output [7:0] out
);

  Multiplexer #(.select(2), .width(8)) multiplexer_1 (
    .in0({Q[7:4], databus[3:0]}), .in1({databus[3:0], Q[3:0]}), .in2(Q), .in3(databus), .out(out), .sel(sel));  // open: en

  // Notes on the sheet:
  //   load R fra dataminne
  //   beholder verdien
  //   load 4 LSB
  //   load 4 MSB
endmodule
